// Logisim project 12hr_clock.circ as structural Verilog: 6 circuits, main circuit Stage4
module Stage2 (
  input  in_1,
  input  Enable__Set,
  input  Set_Time,
  input  in_4
);

  wire and_1_out, and_2_out, and_3_out, and_4_out, and_5_out, and_6_out, and_7_out, button_1_out,
       clock_1_out, j_k_ff_1_q, j_k_ff_2_q, j_k_ff_3_q, j_k_ff_4_q, j_k_ff_5_q, j_k_ff_6_q, j_k_ff_7_q,
       not_1_out, or_1_out;
  wire [2:0] d_ff_1_q;
  wire [3:0] d_ff_4_q;

  J_K_Flip_Flop #(.trigger("falling")) j_k_ff_1 (
    .J(Enable__Set), .K(Enable__Set), .clk(and_7_out), .Q(j_k_ff_1_q), .reset(and_2_out));  // open: Qn, preset
  LED led_1 (.in(j_k_ff_1_q));
  D_Flip_Flop d_ff_1 (.D(j_k_ff_1_q), .clk(or_1_out), .Q(d_ff_1_q[0]));  // open: Qn, preset, reset
  J_K_Flip_Flop #(.trigger("falling")) j_k_ff_2 (
    .J(j_k_ff_1_q), .K(j_k_ff_1_q), .clk(and_7_out), .Q(j_k_ff_2_q), .reset(and_2_out));  // open: Qn, preset
  and and_1 (and_1_out, j_k_ff_1_q, j_k_ff_2_q);
  LED led_2 (.in(j_k_ff_2_q));
  D_Flip_Flop d_ff_2 (.D(j_k_ff_2_q), .clk(or_1_out), .Q(d_ff_1_q[1]));  // open: Qn, preset, reset
  J_K_Flip_Flop #(.trigger("falling")) j_k_ff_3 (
    .J(and_1_out), .K(and_1_out), .clk(and_7_out), .Q(j_k_ff_3_q), .reset(and_2_out));  // open: Qn, preset
  and and_2 (and_2_out, j_k_ff_3_q, j_k_ff_2_q);
  LED led_3 (.in(j_k_ff_3_q));
  D_Flip_Flop d_ff_3 (.D(j_k_ff_3_q), .clk(or_1_out), .Q(d_ff_1_q[2]));  // open: Qn, preset, reset
  Clock clock_1 (.out(clock_1_out));
  Button button_1 (.out(button_1_out));
  not not_1 (not_1_out, Set_Time);
  and and_3 (and_3_out, clock_1_out, not_1_out);
  and and_4 (and_4_out, Set_Time, button_1_out);
  Hex_Digit_Display hex_digit_display_1 (.value({in_4, d_ff_1_q}));  // open: dp
  or or_1 (or_1_out, and_3_out, and_4_out);
  Hex_Digit_Display hex_digit_display_2 (.value(d_ff_4_q));  // open: dp
  J_K_Flip_Flop #(.trigger("falling")) j_k_ff_4 (
    .J(in_1), .K(in_1), .clk(or_1_out), .Q(j_k_ff_4_q), .reset(and_7_out));  // open: Qn, preset
  LED led_4 (.in(j_k_ff_4_q));
  J_K_Flip_Flop #(.trigger("falling")) j_k_ff_5 (
    .J(j_k_ff_4_q), .K(j_k_ff_4_q), .clk(or_1_out), .Q(j_k_ff_5_q), .reset(and_7_out));  // open: Qn, preset
  D_Flip_Flop d_ff_4 (.D(j_k_ff_4_q), .clk(or_1_out), .Q(d_ff_4_q[0]));  // open: Qn, preset, reset
  LED led_5 (.in(j_k_ff_5_q));
  and and_5 (and_5_out, j_k_ff_4_q, j_k_ff_5_q);
  J_K_Flip_Flop #(.trigger("falling")) j_k_ff_6 (
    .J(and_5_out), .K(and_5_out), .clk(or_1_out), .Q(j_k_ff_6_q), .reset(and_7_out));  // open: Qn, preset
  D_Flip_Flop d_ff_5 (.D(j_k_ff_5_q), .clk(or_1_out), .Q(d_ff_4_q[1]));  // open: Qn, preset, reset
  LED led_6 (.in(j_k_ff_6_q));
  and and_6 (and_6_out, and_5_out, j_k_ff_6_q);
  J_K_Flip_Flop #(.trigger("falling")) j_k_ff_7 (
    .J(and_6_out), .K(and_6_out), .clk(or_1_out), .Q(j_k_ff_7_q), .reset(and_7_out));  // open: Qn, preset
  D_Flip_Flop d_ff_6 (.D(j_k_ff_6_q), .clk(or_1_out), .Q(d_ff_4_q[2]));  // open: Qn, preset, reset
  LED led_7 (.in(j_k_ff_7_q));
  D_Flip_Flop d_ff_7 (.D(j_k_ff_7_q), .clk(or_1_out), .Q(d_ff_4_q[3]));  // open: Qn, preset, reset
  and and_7 (and_7_out, j_k_ff_7_q, j_k_ff_5_q);

  // Notes on the sheet:
  //   Q0
  //   Q1
  //   Q2
  //   M+
  //   Clock
  //   Increment time
  //   Q0
  //   1
  //   Q1
  //   2
  //   Q2
  //   4
  //   Q2
  //   8
endmodule

module Stage4 (
  input  Set_Time,
  input  in_2,
  input  Enable__Set,
  input  in_4,
  input  in_5,
  input  in_6,
  input  in_7,
  input  in_8
);

  wire and_1_out, and_2_out, and_3_out, and_4_out, and_5_out, and_6_out, and_7_out, and_8_out, and_9_out,
       and_10_out, and_11_out, and_12_out, and_13_out, and_14_out, and_15_out, and_16_out, button_1_out,
       button_2_out, clock_1_out, j_k_ff_1_q, j_k_ff_2_q, j_k_ff_3_q, j_k_ff_4_q, j_k_ff_5_q, j_k_ff_6_q,
       j_k_ff_7_q, j_k_ff_8_q, j_k_ff_9_q, j_k_ff_10_q, j_k_ff_11_q, j_k_ff_12_q, j_k_ff_13_q, not_1_out,
       not_2_out, not_3_out, not_4_out, not_5_out, not_6_out, not_7_out, not_8_out, not_9_out, or_1_out,
       or_2_out, or_3_out, or_4_out, or_5_out;
  wire [0:0] d_ff_1_q;
  wire [2:0] d_ff_6_q;
  wire [3:0] d_ff_2_q, d_ff_9_q;

  J_K_Flip_Flop j_k_ff_1 (.J(and_1_out), .K(and_1_out), .clk(or_4_out), .Q(j_k_ff_1_q));  // open: Qn, preset, reset
  J_K_Flip_Flop #(.trigger("falling")) j_k_ff_2 (
    .J(not_1_out), .K(not_1_out), .clk(and_7_out), .Q(j_k_ff_2_q), .reset(and_2_out));  // open: Qn, preset
  not not_1 (not_1_out, in_6);
  LED led_1 (.in(j_k_ff_2_q));
  D_Flip_Flop d_ff_1 (.D(j_k_ff_2_q), .clk(or_5_out), .Q(d_ff_1_q[0]));  // open: Qn, preset, reset
  and and_1 (and_1_out, and_3_out, j_k_ff_2_q);
  and and_2 (and_2_out, j_k_ff_2_q, and_4_out);
  J_K_Flip_Flop #(.trigger("falling")) j_k_ff_3 (
    .J(not_2_out), .K(not_2_out), .clk(or_4_out), .Q(j_k_ff_3_q), .reset(and_7_out));  // open: Qn, preset
  not not_2 (not_2_out, in_4);
  LED led_2 (.in(j_k_ff_3_q));
  and and_3 (and_3_out, not_3_out, j_k_ff_4_q);
  not not_3 (not_3_out, j_k_ff_3_q);
  J_K_Flip_Flop #(.trigger("falling")) j_k_ff_4 (
    .J(j_k_ff_3_q), .K(j_k_ff_3_q), .clk(or_4_out), .Q(j_k_ff_4_q), .reset(or_1_out));  // open: Qn, preset
  D_Flip_Flop d_ff_2 (.D(j_k_ff_3_q), .clk(or_5_out), .Q(d_ff_2_q[0]));  // open: Qn, preset, reset
  or or_1 (or_1_out, and_2_out, and_7_out);
  LED led_3 (.in(j_k_ff_4_q));
  and and_4 (and_4_out, j_k_ff_3_q, j_k_ff_4_q, not_4_out, not_5_out);
  and and_5 (and_5_out, j_k_ff_3_q, j_k_ff_4_q);
  J_K_Flip_Flop #(.trigger("falling")) j_k_ff_5 (
    .J(and_5_out), .K(and_5_out), .clk(or_4_out), .Q(j_k_ff_5_q), .reset(or_2_out));  // open: Qn, preset
  D_Flip_Flop d_ff_3 (.D(j_k_ff_4_q), .clk(or_5_out), .Q(d_ff_2_q[1]));  // open: Qn, preset, reset
  not not_4 (not_4_out, j_k_ff_5_q);
  or or_2 (or_2_out, and_2_out, and_7_out);
  LED led_4 (.in(j_k_ff_5_q));
  and and_6 (and_6_out, and_5_out, j_k_ff_5_q);
  J_K_Flip_Flop #(.trigger("falling")) j_k_ff_6 (
    .J(and_6_out), .K(and_6_out), .clk(or_4_out), .Q(j_k_ff_6_q), .reset(or_3_out));  // open: Qn, preset
  D_Flip_Flop d_ff_4 (.D(j_k_ff_5_q), .clk(or_5_out), .Q(d_ff_2_q[2]));  // open: Qn, preset, reset
  not not_5 (not_5_out, j_k_ff_6_q);
  or or_3 (or_3_out, and_2_out, and_7_out);
  LED led_5 (.in(j_k_ff_6_q));
  D_Flip_Flop d_ff_5 (.D(j_k_ff_6_q), .clk(or_5_out), .Q(d_ff_2_q[3]));  // open: Qn, preset, reset
  and and_7 (and_7_out, j_k_ff_6_q, j_k_ff_3_q);
  or or_4 (or_4_out, and_8_out, and_9_out);
  and and_8 (and_8_out, button_1_out, in_5);
  and and_9 (and_9_out, not_6_out, and_11_out);
  LED led_6 (.in(j_k_ff_1_q));
  not not_6 (not_6_out, in_5);
  Button button_1 (.out(button_1_out));
  Hex_Digit_Display hex_digit_display_1 (.value({{3{in_8}}, d_ff_1_q[0]}));  // open: dp
  J_K_Flip_Flop #(.trigger("falling")) j_k_ff_7 (
    .J(not_7_out), .K(not_7_out), .clk(and_16_out), .Q(j_k_ff_7_q), .reset(and_11_out));  // open: Qn, preset
  not not_7 (not_7_out, Enable__Set);
  Hex_Digit_Display hex_digit_display_2 (.value(d_ff_2_q));  // open: dp
  Hex_Digit_Display hex_digit_display_3 (.value({in_7, d_ff_6_q}));  // open: dp
  J_K_Flip_Flop #(.trigger("falling")) j_k_ff_8 (
    .J(j_k_ff_7_q), .K(j_k_ff_7_q), .clk(and_16_out), .Q(j_k_ff_8_q), .reset(and_11_out));  // open: Qn, preset
  LED led_7 (.in(j_k_ff_7_q));
  D_Flip_Flop d_ff_6 (.D(j_k_ff_7_q), .clk(or_5_out), .Q(d_ff_6_q[0]));  // open: Qn, preset, reset
  Hex_Digit_Display hex_digit_display_4 (.value(d_ff_9_q));  // open: dp
  LED led_8 (.in(j_k_ff_8_q));
  and and_10 (and_10_out, j_k_ff_7_q, j_k_ff_8_q);
  J_K_Flip_Flop #(.trigger("falling")) j_k_ff_9 (
    .J(and_10_out), .K(and_10_out), .clk(and_16_out), .Q(j_k_ff_9_q), .reset(and_11_out));  // open: Qn, preset
  D_Flip_Flop d_ff_7 (.D(j_k_ff_8_q), .clk(or_5_out), .Q(d_ff_6_q[1]));  // open: Qn, preset, reset
  LED led_9 (.in(j_k_ff_9_q));
  and and_11 (and_11_out, j_k_ff_9_q, j_k_ff_8_q);
  D_Flip_Flop d_ff_8 (.D(j_k_ff_9_q), .clk(or_5_out), .Q(d_ff_6_q[2]));  // open: Qn, preset, reset
  Clock clock_1 (.out(clock_1_out));
  not not_8 (not_8_out, Set_Time);
  Button button_2 (.out(button_2_out));
  and and_12 (and_12_out, clock_1_out, not_8_out);
  and and_13 (and_13_out, Set_Time, button_2_out);
  or or_5 (or_5_out, and_12_out, and_13_out);
  J_K_Flip_Flop #(.trigger("falling")) j_k_ff_10 (
    .J(not_9_out), .K(not_9_out), .clk(or_5_out), .Q(j_k_ff_10_q), .reset(and_16_out));  // open: Qn, preset
  not not_9 (not_9_out, in_2);
  LED led_10 (.in(j_k_ff_10_q));
  J_K_Flip_Flop #(.trigger("falling")) j_k_ff_11 (
    .J(j_k_ff_10_q), .K(j_k_ff_10_q), .clk(or_5_out), .Q(j_k_ff_11_q), .reset(and_16_out));  // open: Qn, preset
  D_Flip_Flop d_ff_9 (.D(j_k_ff_10_q), .clk(or_5_out), .Q(d_ff_9_q[0]));  // open: Qn, preset, reset
  LED led_11 (.in(j_k_ff_11_q));
  and and_14 (and_14_out, j_k_ff_10_q, j_k_ff_11_q);
  J_K_Flip_Flop #(.trigger("falling")) j_k_ff_12 (
    .J(and_14_out), .K(and_14_out), .clk(or_5_out), .Q(j_k_ff_12_q), .reset(and_16_out));  // open: Qn, preset
  D_Flip_Flop d_ff_10 (.D(j_k_ff_11_q), .clk(or_5_out), .Q(d_ff_9_q[1]));  // open: Qn, preset, reset
  LED led_12 (.in(j_k_ff_12_q));
  and and_15 (and_15_out, and_14_out, j_k_ff_12_q);
  J_K_Flip_Flop #(.trigger("falling")) j_k_ff_13 (
    .J(and_15_out), .K(and_15_out), .clk(or_5_out), .Q(j_k_ff_13_q), .reset(and_16_out));  // open: Qn, preset
  D_Flip_Flop d_ff_11 (.D(j_k_ff_12_q), .clk(or_5_out), .Q(d_ff_9_q[2]));  // open: Qn, preset, reset
  LED led_13 (.in(j_k_ff_13_q));
  D_Flip_Flop d_ff_12 (.D(j_k_ff_13_q), .clk(or_5_out), .Q(d_ff_9_q[3]));  // open: Qn, preset, reset
  and and_16 (and_16_out, j_k_ff_13_q, j_k_ff_11_q);

  // Notes on the sheet:
  //   Q2
  //   Full Reset
  //   Q0
  //   1
  //   Q1
  //   2
  //   Q2
  //   4
  //   Q2
  //   8
  //   OFF = AM
  //   ON = PM
  //   Connect the 2 set time modes
  //   Increment time
  //   H+
  //   Q0
  //   Q1
  //   Q2
  //   Connect the 2 set time modes
  //   Clock
  //   M+
  //   Increment time
  //   Enable (Set)
  //   Q0
  //   1
  //   Q1
  //   2
  //   Q2
  //   4
  //   Q2
  //   8
endmodule

module Stage3 (
  input  Set_Time,
  input  in_2,
  input  in_3,
  input  in_4
);

  wire and_1_out, and_2_out, and_3_out, and_4_out, and_5_out, and_6_out, and_7_out, and_8_out, and_9_out,
       button_1_out, clock_1_out, j_k_ff_1_q, j_k_ff_2_q, j_k_ff_3_q, j_k_ff_4_q, j_k_ff_5_q, j_k_ff_6_q,
       not_1_out, not_2_out, not_3_out, not_4_out, or_1_out, or_2_out, or_3_out, or_4_out;
  wire [0:0] d_ff_1_q;
  wire [3:0] d_ff_2_q;

  J_K_Flip_Flop j_k_ff_1 (.J(and_1_out), .K(and_1_out), .clk(or_4_out), .Q(j_k_ff_1_q));  // open: Qn, preset, reset
  J_K_Flip_Flop #(.trigger("falling")) j_k_ff_2 (
    .J(in_3), .K(in_3), .clk(and_7_out), .Q(j_k_ff_2_q), .reset(and_2_out));  // open: Qn, preset
  LED led_1 (.in(j_k_ff_2_q));
  D_Flip_Flop d_ff_1 (.D(j_k_ff_2_q), .clk(or_4_out), .Q(d_ff_1_q[0]));  // open: Qn, preset, reset
  and and_1 (and_1_out, and_3_out, j_k_ff_2_q);
  and and_2 (and_2_out, j_k_ff_2_q, and_4_out);
  J_K_Flip_Flop #(.trigger("falling")) j_k_ff_3 (
    .J(in_2), .K(in_2), .clk(or_4_out), .Q(j_k_ff_3_q), .reset(and_7_out));  // open: Qn, preset
  LED led_2 (.in(j_k_ff_3_q));
  and and_3 (and_3_out, not_1_out, j_k_ff_4_q);
  not not_1 (not_1_out, j_k_ff_3_q);
  J_K_Flip_Flop #(.trigger("falling")) j_k_ff_4 (
    .J(j_k_ff_3_q), .K(j_k_ff_3_q), .clk(or_4_out), .Q(j_k_ff_4_q), .reset(or_1_out));  // open: Qn, preset
  D_Flip_Flop d_ff_2 (.D(j_k_ff_3_q), .clk(or_4_out), .Q(d_ff_2_q[0]));  // open: Qn, preset, reset
  or or_1 (or_1_out, and_2_out, and_7_out);
  LED led_3 (.in(j_k_ff_4_q));
  LED led_4 (.in(j_k_ff_1_q));
  and and_4 (and_4_out, j_k_ff_3_q, j_k_ff_4_q, not_2_out, not_3_out);
  and and_5 (and_5_out, j_k_ff_3_q, j_k_ff_4_q);
  J_K_Flip_Flop #(.trigger("falling")) j_k_ff_5 (
    .J(and_5_out), .K(and_5_out), .clk(or_4_out), .Q(j_k_ff_5_q), .reset(or_2_out));  // open: Qn, preset
  D_Flip_Flop d_ff_3 (.D(j_k_ff_4_q), .clk(or_4_out), .Q(d_ff_2_q[1]));  // open: Qn, preset, reset
  Hex_Digit_Display hex_digit_display_1 (.value({{3{in_4}}, d_ff_1_q[0]}));  // open: dp
  Hex_Digit_Display hex_digit_display_2 (.value(d_ff_2_q));  // open: dp
  not not_2 (not_2_out, j_k_ff_5_q);
  or or_2 (or_2_out, and_2_out, and_7_out);
  LED led_5 (.in(j_k_ff_5_q));
  and and_6 (and_6_out, and_5_out, j_k_ff_5_q);
  J_K_Flip_Flop #(.trigger("falling")) j_k_ff_6 (
    .J(and_6_out), .K(and_6_out), .clk(or_4_out), .Q(j_k_ff_6_q), .reset(or_3_out));  // open: Qn, preset
  D_Flip_Flop d_ff_4 (.D(j_k_ff_5_q), .clk(or_4_out), .Q(d_ff_2_q[2]));  // open: Qn, preset, reset
  not not_3 (not_3_out, j_k_ff_6_q);
  or or_3 (or_3_out, and_2_out, and_7_out);
  LED led_6 (.in(j_k_ff_6_q));
  D_Flip_Flop d_ff_5 (.D(j_k_ff_6_q), .clk(or_4_out), .Q(d_ff_2_q[3]));  // open: Qn, preset, reset
  and and_7 (and_7_out, j_k_ff_6_q, j_k_ff_3_q);
  Clock clock_1 (.out(clock_1_out));
  Button button_1 (.out(button_1_out));
  not not_4 (not_4_out, Set_Time);
  and and_8 (and_8_out, clock_1_out, not_4_out);
  and and_9 (and_9_out, Set_Time, button_1_out);
  or or_4 (or_4_out, and_8_out, and_9_out);

  // Notes on the sheet:
  //   Q2
  //   Full Reset
  //   Q0
  //   1
  //   AM/PM
  //   Q1
  //   2
  //   Q2
  //   4
  //   Q2
  //   8
  //   H+
  //   Clock
  //   Increment time
endmodule

module Stage_5_Double_Clock (
  input  in_1,
  input  in_2,
  input  in_3,
  input  Enable__Set,
  input  Set_Time,
  input  in_6,
  input  Set_Alarm,
  input  in_8,
  input  in_9,
  input  in_10,
  input  Enable__Set_2,
  input  in_12,
  input  in_13
);

  wire and_1_out, and_2_out, and_3_out, and_4_out, and_5_out, and_6_out, and_7_out, and_8_out, and_9_out,
       and_10_out, and_11_out, and_12_out, and_13_out, and_14_out, and_15_out, and_16_out, and_17_out,
       and_18_out, and_19_out, and_20_out, and_21_out, and_22_out, and_23_out, and_24_out, and_25_out,
       and_26_out, and_27_out, and_28_out, and_29_out, and_30_out, and_31_out, and_32_out, and_33_out,
       and_34_out, and_35_out, and_36_out, and_37_out, and_38_out, and_39_out, and_40_out, and_41_out,
       and_42_out, and_43_out, and_44_out, and_45_out, and_46_out, and_47_out, and_48_out, and_49_out,
       and_50_out, and_51_out, and_52_out, and_53_out, and_54_out, and_55_out, and_56_out, and_57_out,
       and_58_out, and_59_out, and_60_out, and_61_out, and_62_out, and_63_out, and_64_out, and_65_out,
       and_66_out, and_67_out, and_68_out, and_69_out, and_70_out, and_71_out, and_72_out, and_73_out,
       and_74_out, and_75_out, and_76_out, and_77_out, and_78_out, and_79_out, and_80_out, and_81_out,
       and_82_out, and_83_out, and_84_out, and_85_out, and_86_out, and_87_out, and_88_out, and_89_out,
       and_90_out, and_91_out, and_92_out, and_93_out, and_94_out, button_1_out, button_2_out, button_3_out,
       clock_1_out, clock_2_out, clock_3_out, d_ff_1_q, d_ff_2_q, d_ff_3_q, d_ff_4_q, d_ff_5_q, d_ff_6_q,
       d_ff_7_q, d_ff_8_q, d_ff_9_q, d_ff_10_q, d_ff_11_q, d_ff_12_q, d_ff_13_q, d_ff_14_q, d_ff_15_q,
       d_ff_16_q, d_ff_17_q, d_ff_18_q, d_ff_19_q, d_ff_20_q, d_ff_21_q, d_ff_22_q, d_ff_23_q, d_ff_24_q,
       j_k_ff_1_q, j_k_ff_2_q, j_k_ff_3_q, j_k_ff_4_q, j_k_ff_5_q, j_k_ff_6_q, j_k_ff_7_q, j_k_ff_8_q,
       j_k_ff_9_q, j_k_ff_10_q, j_k_ff_11_q, j_k_ff_12_q, j_k_ff_13_q, j_k_ff_14_q, j_k_ff_15_q, j_k_ff_16_q,
       j_k_ff_17_q, j_k_ff_18_q, j_k_ff_19_q, j_k_ff_20_q, j_k_ff_21_q, j_k_ff_22_q, j_k_ff_23_q,
       j_k_ff_24_q, j_k_ff_25_q, j_k_ff_26_q, j_k_ff_27_q, not_1_out, not_2_out, not_3_out, not_4_out,
       not_5_out, not_6_out, not_7_out, not_8_out, not_9_out, not_10_out, not_11_out, not_12_out, not_13_out,
       not_14_out, not_15_out, not_16_out, not_17_out, not_18_out, not_19_out, not_20_out, not_21_out,
       not_22_out, not_23_out, not_24_out, not_25_out, not_26_out, not_27_out, not_28_out, not_29_out,
       not_30_out, not_31_out, not_32_out, not_33_out, not_34_out, not_35_out, not_36_out, not_37_out,
       not_38_out, not_39_out, not_40_out, not_41_out, not_42_out, not_43_out, not_44_out, not_45_out,
       not_46_out, not_47_out, not_48_out, not_49_out, not_50_out, not_51_out, not_52_out, not_53_out,
       not_54_out, not_55_out, not_56_out, not_57_out, not_58_out, not_59_out, not_60_out, or_1_out,
       or_2_out, or_3_out, or_5_out, or_6_out, or_8_out, or_9_out, or_11_out, or_12_out, or_14_out,
       or_15_out, or_16_out, or_18_out, or_19_out, or_20_out, or_22_out, or_24_out, or_26_out, or_28_out,
       or_29_out, or_32_out, or_34_out, or_35_out, or_36_out, or_37_out;
  wire [0:0] or_4_out;
  wire [2:0] or_21_out;
  wire [3:0] or_7_out, or_27_out;

  J_K_Flip_Flop j_k_ff_1 (.J(and_7_out), .K(and_7_out), .clk(or_20_out), .Q(j_k_ff_1_q));  // open: Qn, preset, reset
  J_K_Flip_Flop #(.trigger("falling")) j_k_ff_2 (
    .J(not_1_out), .K(not_1_out), .clk(and_39_out), .Q(j_k_ff_2_q), .reset(and_12_out));  // open: Qn, preset
  not not_1 (not_1_out, in_13);
  not not_2 (not_2_out, Set_Alarm);
  and and_1 (and_1_out, j_k_ff_3_q, not_2_out);
  and and_2 (and_2_out, Set_Alarm, j_k_ff_1_q);
  or or_1 (or_1_out, and_1_out, and_2_out);
  or or_2 (or_2_out, and_3_out, and_4_out);
  and and_3 (and_3_out, not_3_out, not_4_out);
  and and_4 (and_4_out, j_k_ff_3_q, j_k_ff_1_q);
  not not_3 (not_3_out, j_k_ff_3_q);
  not not_4 (not_4_out, j_k_ff_1_q);
  LED led_1 (.in(j_k_ff_2_q));
  D_Flip_Flop d_ff_1 (.D(j_k_ff_2_q), .clk(clock_2_out), .Q(d_ff_1_q));  // open: Qn, preset, reset
  J_K_Flip_Flop j_k_ff_3 (.J(and_8_out), .K(and_8_out), .clk(or_19_out), .Q(j_k_ff_3_q));  // open: Qn, preset, reset
  J_K_Flip_Flop #(.trigger("falling")) j_k_ff_4 (
    .J(not_5_out), .K(not_5_out), .clk(and_40_out), .Q(j_k_ff_4_q), .reset(and_13_out));  // open: Qn, preset
  not not_5 (not_5_out, in_3);
  and and_5 (and_5_out, or_2_out, or_3_out);
  or or_3 (or_3_out, and_6_out, and_11_out);
  and and_6 (and_6_out, not_6_out, not_7_out);
  not not_6 (not_6_out, d_ff_2_q);
  not not_7 (not_7_out, d_ff_1_q);
  and and_7 (and_7_out, and_15_out, j_k_ff_2_q);
  and and_8 (and_8_out, and_14_out, j_k_ff_4_q);
  LED led_2 (.in(j_k_ff_4_q));
  D_Flip_Flop d_ff_2 (.D(j_k_ff_4_q), .clk(or_35_out), .Q(d_ff_2_q));  // open: Qn, preset, reset
  not not_8 (not_8_out, Set_Alarm);
  and and_9 (and_9_out, d_ff_2_q, not_8_out);
  and and_10 (and_10_out, Set_Alarm, d_ff_1_q);
  or or_4 (or_4_out[0], and_9_out, and_10_out);
  and and_11 (and_11_out, d_ff_2_q, d_ff_1_q);
  and and_12 (and_12_out, j_k_ff_2_q, and_27_out);
  and and_13 (and_13_out, j_k_ff_4_q, and_21_out);
  not not_9 (not_9_out, in_12);
  J_K_Flip_Flop #(.trigger("falling")) j_k_ff_5 (
    .J(not_10_out), .K(not_10_out), .clk(or_19_out), .Q(j_k_ff_5_q), .reset(and_40_out));  // open: Qn, preset
  not not_10 (not_10_out, in_1);
  J_K_Flip_Flop #(.trigger("falling")) j_k_ff_6 (
    .J(not_9_out), .K(not_9_out), .clk(or_20_out), .Q(j_k_ff_6_q), .reset(and_39_out));  // open: Qn, preset
  LED led_3 (.in(j_k_ff_5_q));
  D_Flip_Flop d_ff_3 (.D(j_k_ff_5_q), .clk(or_35_out), .Q(d_ff_3_q));  // open: Qn, preset, reset
  not not_11 (not_11_out, j_k_ff_6_q);
  LED led_4 (.in(j_k_ff_6_q));
  D_Flip_Flop d_ff_4 (.D(j_k_ff_6_q), .clk(clock_2_out), .Q(d_ff_4_q));  // open: Qn, preset, reset
  and and_14 (and_14_out, not_12_out, j_k_ff_7_q);
  not not_12 (not_12_out, j_k_ff_5_q);
  J_K_Flip_Flop #(.trigger("falling")) j_k_ff_7 (
    .J(j_k_ff_5_q), .K(j_k_ff_5_q), .clk(or_19_out), .Q(j_k_ff_7_q), .reset(or_5_out));  // open: Qn, preset
  or or_5 (or_5_out, and_13_out, and_40_out);
  not not_13 (not_13_out, d_ff_3_q);
  and and_15 (and_15_out, not_11_out, j_k_ff_8_q);
  J_K_Flip_Flop #(.trigger("falling")) j_k_ff_8 (
    .J(j_k_ff_6_q), .K(j_k_ff_6_q), .clk(or_20_out), .Q(j_k_ff_8_q), .reset(or_6_out));  // open: Qn, preset
  or or_6 (or_6_out, and_12_out, and_39_out);
  LED led_5 (.in(j_k_ff_7_q));
  D_Flip_Flop d_ff_5 (.D(j_k_ff_7_q), .clk(or_35_out), .Q(d_ff_5_q));  // open: Qn, preset, reset
  not not_14 (not_14_out, Set_Alarm);
  and and_16 (and_16_out, d_ff_3_q, not_14_out);
  and and_17 (and_17_out, Set_Alarm, d_ff_4_q);
  or or_7 (or_7_out[0], and_16_out, and_17_out);
  or or_8 (or_8_out, and_18_out, and_19_out);
  and and_18 (and_18_out, not_13_out, not_15_out);
  and and_19 (and_19_out, d_ff_3_q, d_ff_4_q);
  not not_15 (not_15_out, d_ff_4_q);
  and and_20 (and_20_out, j_k_ff_6_q, j_k_ff_8_q);
  LED led_6 (.in(j_k_ff_8_q));
  D_Flip_Flop d_ff_6 (.D(j_k_ff_8_q), .clk(clock_2_out), .Q(d_ff_6_q));  // open: Qn, preset, reset
  and and_21 (and_21_out, j_k_ff_5_q, j_k_ff_7_q, not_16_out, not_24_out);
  not not_16 (not_16_out, j_k_ff_9_q);
  and and_22 (and_22_out, j_k_ff_5_q, j_k_ff_7_q);
  J_K_Flip_Flop #(.trigger("falling")) j_k_ff_9 (
    .J(and_22_out), .K(and_22_out), .clk(or_19_out), .Q(j_k_ff_9_q), .reset(or_9_out));  // open: Qn, preset
  or or_9 (or_9_out, and_13_out, and_40_out);
  not not_17 (not_17_out, Set_Alarm);
  and and_23 (and_23_out, d_ff_5_q, not_17_out);
  and and_24 (and_24_out, Set_Alarm, d_ff_6_q);
  or or_10 (or_7_out[1], and_23_out, and_24_out);
  or or_11 (or_11_out, and_25_out, and_26_out);
  and and_25 (and_25_out, not_18_out, not_19_out);
  and and_26 (and_26_out, d_ff_5_q, d_ff_6_q);
  not not_18 (not_18_out, d_ff_5_q);
  not not_19 (not_19_out, d_ff_6_q);
  and and_27 (and_27_out, j_k_ff_6_q, j_k_ff_8_q, not_20_out, not_27_out);
  not not_20 (not_20_out, j_k_ff_10_q);
  J_K_Flip_Flop #(.trigger("falling")) j_k_ff_10 (
    .J(and_20_out), .K(and_20_out), .clk(or_20_out), .Q(j_k_ff_10_q), .reset(or_12_out));  // open: Qn, preset
  or or_12 (or_12_out, and_12_out, and_39_out);
  LED led_7 (.in(j_k_ff_9_q));
  D_Flip_Flop d_ff_7 (.D(j_k_ff_9_q), .clk(or_35_out), .Q(d_ff_7_q));  // open: Qn, preset, reset
  not not_21 (not_21_out, Set_Alarm);
  and and_28 (and_28_out, d_ff_7_q, not_21_out);
  or or_13 (or_7_out[2], and_28_out, and_33_out);
  and and_29 (and_29_out, or_8_out, or_11_out, or_14_out, or_18_out);
  or or_14 (or_14_out, and_30_out, and_36_out);
  and and_30 (and_30_out, not_22_out, not_23_out);
  not not_22 (not_22_out, d_ff_7_q);
  not not_23 (not_23_out, d_ff_8_q);
  and and_31 (and_31_out, and_20_out, j_k_ff_10_q);
  LED led_8 (.in(j_k_ff_10_q));
  D_Flip_Flop d_ff_8 (.D(j_k_ff_10_q), .clk(clock_2_out), .Q(d_ff_8_q));  // open: Qn, preset, reset
  not not_24 (not_24_out, j_k_ff_11_q);
  and and_32 (and_32_out, and_22_out, j_k_ff_9_q);
  J_K_Flip_Flop #(.trigger("falling")) j_k_ff_11 (
    .J(and_32_out), .K(and_32_out), .clk(or_19_out), .Q(j_k_ff_11_q), .reset(or_15_out));  // open: Qn, preset
  or or_15 (or_15_out, and_13_out, and_40_out);
  and and_33 (and_33_out, Set_Alarm, d_ff_8_q);
  and and_34 (and_34_out, d_ff_9_q, not_28_out);
  and and_35 (and_35_out, not_25_out, not_26_out);
  and and_36 (and_36_out, d_ff_7_q, d_ff_8_q);
  not not_25 (not_25_out, d_ff_9_q);
  not not_26 (not_26_out, d_ff_10_q);
  not not_27 (not_27_out, j_k_ff_12_q);
  J_K_Flip_Flop #(.trigger("falling")) j_k_ff_12 (
    .J(and_31_out), .K(and_31_out), .clk(or_20_out), .Q(j_k_ff_12_q), .reset(or_16_out));  // open: Qn, preset
  or or_16 (or_16_out, and_12_out, and_39_out);
  LED led_9 (.in(j_k_ff_11_q));
  D_Flip_Flop d_ff_9 (.D(j_k_ff_11_q), .clk(or_35_out), .Q(d_ff_9_q));  // open: Qn, preset, reset
  not not_28 (not_28_out, Set_Alarm);
  and and_37 (and_37_out, Set_Alarm, d_ff_10_q);
  or or_17 (or_7_out[3], and_34_out, and_37_out);
  or or_18 (or_18_out, and_35_out, and_38_out);
  and and_38 (and_38_out, d_ff_9_q, d_ff_10_q);
  and and_39 (and_39_out, j_k_ff_12_q, j_k_ff_8_q);
  LED led_10 (.in(j_k_ff_12_q));
  D_Flip_Flop d_ff_10 (.D(j_k_ff_12_q), .clk(clock_2_out), .Q(d_ff_10_q));  // open: Qn, preset, reset
  and and_40 (and_40_out, j_k_ff_11_q, j_k_ff_7_q);
  or or_19 (or_19_out, and_85_out, and_55_out);
  or or_20 (or_20_out, and_90_out, and_58_out);
  and and_41 (and_41_out, and_5_out, and_29_out);
  not not_29 (not_29_out, Enable__Set_2);
  J_K_Flip_Flop #(.trigger("falling")) j_k_ff_13 (
    .J(not_30_out), .K(not_30_out), .clk(and_77_out), .Q(j_k_ff_13_q), .reset(and_55_out));  // open: Qn, preset
  not not_30 (not_30_out, Enable__Set);
  J_K_Flip_Flop #(.trigger("falling")) j_k_ff_14 (
    .J(not_29_out), .K(not_29_out), .clk(and_84_out), .Q(j_k_ff_14_q), .reset(and_58_out));  // open: Qn, preset
  LED led_11 (.in(j_k_ff_13_q));
  D_Flip_Flop d_ff_11 (.D(j_k_ff_13_q), .clk(or_35_out), .Q(d_ff_11_q));  // open: Qn, preset, reset
  LED led_12 (.in(j_k_ff_14_q));
  D_Flip_Flop d_ff_12 (.D(j_k_ff_14_q), .clk(clock_2_out), .Q(d_ff_12_q));  // open: Qn, preset, reset
  J_K_Flip_Flop #(.trigger("falling")) j_k_ff_15 (
    .J(j_k_ff_13_q), .K(j_k_ff_13_q), .clk(and_77_out), .Q(j_k_ff_15_q), .reset(and_55_out));  // open: Qn, preset
  J_K_Flip_Flop #(.trigger("falling")) j_k_ff_16 (
    .J(j_k_ff_14_q), .K(j_k_ff_14_q), .clk(and_84_out), .Q(j_k_ff_16_q), .reset(and_58_out));  // open: Qn, preset
  LED led_13 (.in(j_k_ff_15_q));
  D_Flip_Flop d_ff_13 (.D(j_k_ff_15_q), .clk(or_35_out), .Q(d_ff_13_q));  // open: Qn, preset, reset
  not not_31 (not_31_out, Set_Alarm);
  and and_42 (and_42_out, d_ff_11_q, not_31_out);
  and and_43 (and_43_out, Set_Alarm, d_ff_12_q);
  or or_21 (or_21_out[0], and_42_out, and_43_out);
  or or_22 (or_22_out, and_44_out, and_45_out);
  and and_44 (and_44_out, not_32_out, not_33_out);
  and and_45 (and_45_out, d_ff_11_q, d_ff_12_q);
  not not_32 (not_32_out, d_ff_11_q);
  not not_33 (not_33_out, d_ff_12_q);
  LED led_14 (.in(j_k_ff_16_q));
  D_Flip_Flop d_ff_14 (.D(j_k_ff_16_q), .clk(clock_2_out), .Q(d_ff_14_q));  // open: Qn, preset, reset
  and and_46 (and_46_out, j_k_ff_13_q, j_k_ff_15_q);
  J_K_Flip_Flop #(.trigger("falling")) j_k_ff_17 (
    .J(and_46_out), .K(and_46_out), .clk(and_77_out), .Q(j_k_ff_17_q), .reset(and_55_out));  // open: Qn, preset
  not not_34 (not_34_out, Set_Alarm);
  and and_47 (and_47_out, d_ff_13_q, not_34_out);
  or or_23 (or_21_out[1], and_47_out, and_51_out);
  and and_48 (and_48_out, or_22_out, or_24_out, or_26_out);
  or or_24 (or_24_out, and_49_out, and_54_out);
  and and_49 (and_49_out, not_35_out, not_36_out);
  not not_35 (not_35_out, d_ff_13_q);
  not not_36 (not_36_out, d_ff_14_q);
  and and_50 (and_50_out, j_k_ff_14_q, j_k_ff_16_q);
  J_K_Flip_Flop #(.trigger("falling")) j_k_ff_18 (
    .J(and_50_out), .K(and_50_out), .clk(and_84_out), .Q(j_k_ff_18_q), .reset(and_58_out));  // open: Qn, preset
  LED led_15 (.in(j_k_ff_17_q));
  D_Flip_Flop d_ff_15 (.D(j_k_ff_17_q), .clk(or_35_out), .Q(d_ff_15_q));  // open: Qn, preset, reset
  and and_51 (and_51_out, Set_Alarm, d_ff_14_q);
  and and_52 (and_52_out, d_ff_15_q, not_38_out);
  and and_53 (and_53_out, not_37_out, not_39_out);
  and and_54 (and_54_out, d_ff_13_q, d_ff_14_q);
  not not_37 (not_37_out, d_ff_15_q);
  LED led_16 (.in(j_k_ff_18_q));
  D_Flip_Flop d_ff_16 (.D(j_k_ff_18_q), .clk(clock_2_out), .Q(d_ff_16_q));  // open: Qn, preset, reset
  and and_55 (and_55_out, j_k_ff_17_q, j_k_ff_15_q);
  not not_38 (not_38_out, Set_Alarm);
  and and_56 (and_56_out, Set_Alarm, d_ff_16_q);
  or or_25 (or_21_out[2], and_52_out, and_56_out);
  or or_26 (or_26_out, and_53_out, and_57_out);
  and and_57 (and_57_out, d_ff_15_q, d_ff_16_q);
  not not_39 (not_39_out, d_ff_16_q);
  and and_58 (and_58_out, j_k_ff_18_q, j_k_ff_16_q);
  and and_59 (and_59_out, and_41_out, and_48_out);
  J_K_Flip_Flop #(.trigger("falling")) j_k_ff_19 (
    .J(not_40_out), .K(not_40_out), .clk(and_88_out), .Q(j_k_ff_19_q), .reset(and_77_out));  // open: Qn, preset
  not not_40 (not_40_out, in_2);
  not not_41 (not_41_out, in_10);
  LED led_17 (.in(j_k_ff_19_q));
  J_K_Flip_Flop #(.trigger("falling")) j_k_ff_20 (
    .J(not_41_out), .K(not_41_out), .clk(and_89_out), .Q(j_k_ff_20_q), .reset(and_84_out));  // open: Qn, preset
  J_K_Flip_Flop #(.trigger("falling")) j_k_ff_21 (
    .J(j_k_ff_19_q), .K(j_k_ff_19_q), .clk(and_88_out), .Q(j_k_ff_21_q), .reset(and_77_out));  // open: Qn, preset
  D_Flip_Flop d_ff_17 (.D(j_k_ff_19_q), .clk(or_35_out), .Q(d_ff_17_q));  // open: Qn, preset, reset
  LED led_18 (.in(j_k_ff_20_q));
  D_Flip_Flop d_ff_18 (.D(j_k_ff_20_q), .clk(clock_2_out), .Q(d_ff_18_q));  // open: Qn, preset, reset
  LED led_19 (.in(j_k_ff_21_q));
  J_K_Flip_Flop #(.trigger("falling")) j_k_ff_22 (
    .J(j_k_ff_20_q), .K(j_k_ff_20_q), .clk(and_89_out), .Q(j_k_ff_22_q), .reset(and_84_out));  // open: Qn, preset
  and and_60 (and_60_out, j_k_ff_19_q, j_k_ff_21_q);
  J_K_Flip_Flop #(.trigger("falling")) j_k_ff_23 (
    .J(and_60_out), .K(and_60_out), .clk(and_88_out), .Q(j_k_ff_23_q), .reset(and_77_out));  // open: Qn, preset
  D_Flip_Flop d_ff_19 (.D(j_k_ff_21_q), .clk(or_35_out), .Q(d_ff_19_q));  // open: Qn, preset, reset
  not not_42 (not_42_out, Set_Alarm);
  and and_61 (and_61_out, d_ff_17_q, not_42_out);
  or or_27 (or_27_out[0], and_61_out, and_65_out);
  or or_28 (or_28_out, and_62_out, and_63_out);
  and and_62 (and_62_out, not_43_out, not_44_out);
  and and_63 (and_63_out, d_ff_17_q, d_ff_18_q);
  not not_43 (not_43_out, d_ff_17_q);
  not not_44 (not_44_out, d_ff_18_q);
  and and_64 (and_64_out, j_k_ff_20_q, j_k_ff_22_q);
  LED led_20 (.in(j_k_ff_22_q));
  D_Flip_Flop d_ff_20 (.D(j_k_ff_22_q), .clk(clock_2_out), .Q(d_ff_20_q));  // open: Qn, preset, reset
  LED led_21 (.in(j_k_ff_23_q));
  and and_65 (and_65_out, Set_Alarm, d_ff_18_q);
  and and_66 (and_66_out, d_ff_19_q, not_47_out);
  or or_29 (or_29_out, and_67_out, and_72_out);
  and and_67 (and_67_out, not_45_out, not_46_out);
  not not_45 (not_45_out, d_ff_19_q);
  not not_46 (not_46_out, d_ff_20_q);
  J_K_Flip_Flop #(.trigger("falling")) j_k_ff_24 (
    .J(and_64_out), .K(and_64_out), .clk(and_89_out), .Q(j_k_ff_24_q), .reset(and_84_out));  // open: Qn, preset
  and and_68 (and_68_out, and_60_out, j_k_ff_23_q);
  J_K_Flip_Flop #(.trigger("falling")) j_k_ff_25 (
    .J(and_68_out), .K(and_68_out), .clk(and_88_out), .Q(j_k_ff_25_q), .reset(and_77_out));  // open: Qn, preset
  D_Flip_Flop d_ff_21 (.D(j_k_ff_23_q), .clk(or_35_out), .Q(d_ff_21_q));  // open: Qn, preset, reset
  not not_47 (not_47_out, Set_Alarm);
  and and_69 (and_69_out, Set_Alarm, d_ff_20_q);
  or or_30 (or_27_out[1], and_66_out, and_69_out);
  and and_70 (and_70_out, or_28_out, or_29_out, or_32_out, or_34_out);
  and and_71 (and_71_out, not_48_out, not_50_out);
  and and_72 (and_72_out, d_ff_19_q, d_ff_20_q);
  not not_48 (not_48_out, d_ff_21_q);
  and and_73 (and_73_out, and_64_out, j_k_ff_24_q);
  LED led_22 (.in(j_k_ff_24_q));
  D_Flip_Flop d_ff_22 (.D(j_k_ff_24_q), .clk(clock_2_out), .Q(d_ff_22_q));  // open: Qn, preset, reset
  LED led_23 (.in(j_k_ff_25_q));
  D_Flip_Flop d_ff_23 (.D(j_k_ff_25_q), .clk(or_35_out), .Q(d_ff_23_q));  // open: Qn, preset, reset
  not not_49 (not_49_out, Set_Alarm);
  and and_74 (and_74_out, d_ff_21_q, not_49_out);
  and and_75 (and_75_out, Set_Alarm, d_ff_22_q);
  or or_31 (or_27_out[2], and_74_out, and_75_out);
  or or_32 (or_32_out, and_71_out, and_76_out);
  and and_76 (and_76_out, d_ff_21_q, d_ff_22_q);
  not not_50 (not_50_out, d_ff_22_q);
  J_K_Flip_Flop #(.trigger("falling")) j_k_ff_26 (
    .J(and_73_out), .K(and_73_out), .clk(and_89_out), .Q(j_k_ff_26_q), .reset(and_84_out));  // open: Qn, preset
  and and_77 (and_77_out, j_k_ff_25_q, j_k_ff_21_q);
  not not_51 (not_51_out, Set_Alarm);
  and and_78 (and_78_out, d_ff_23_q, not_51_out);
  and and_79 (and_79_out, Set_Alarm, d_ff_24_q);
  or or_33 (or_27_out[3], and_78_out, and_79_out);
  or or_34 (or_34_out, and_80_out, and_81_out);
  and and_80 (and_80_out, not_52_out, not_53_out);
  and and_81 (and_81_out, d_ff_23_q, d_ff_24_q);
  not not_52 (not_52_out, d_ff_23_q);
  not not_53 (not_53_out, d_ff_24_q);
  LED led_24 (.in(j_k_ff_26_q));
  D_Flip_Flop d_ff_24 (.D(j_k_ff_26_q), .clk(clock_2_out), .Q(d_ff_24_q));  // open: Qn, preset, reset
  Clock clock_1 (.out(clock_1_out));
  not not_54 (not_54_out, Set_Time);
  and and_82 (and_82_out, and_88_out, not_54_out);
  and and_83 (and_83_out, Set_Time, clock_1_out);
  or or_35 (or_35_out, and_82_out, and_83_out);
  and and_84 (and_84_out, j_k_ff_26_q, j_k_ff_22_q);
  Clock clock_2 (.out(clock_2_out));
  and and_85 (and_85_out, Set_Time, and_87_out);
  and and_86 (and_86_out, and_59_out, and_70_out);
  and and_87 (and_87_out, not_55_out, button_2_out);
  and and_88 (and_88_out, not_56_out, or_37_out);
  and and_89 (and_89_out, button_1_out, Set_Alarm);
  and and_90 (and_90_out, button_2_out, Set_Alarm);
  or or_36 (or_36_out, not_58_out, and_93_out);
  not not_55 (not_55_out, Set_Alarm);
  not not_56 (not_56_out, Set_Alarm);
  or or_37 (or_37_out, and_91_out, and_92_out);
  and and_91 (and_91_out, clock_3_out, not_57_out);
  not not_57 (not_57_out, Set_Time);
  and and_92 (and_92_out, Set_Time, button_1_out);
  and and_93 (and_93_out, in_6, button_3_out);
  not not_58 (not_58_out, in_6);
  Clock #(.highDuration(4), .lowDuration(4)) clock_3 (.out(clock_3_out));
  Button button_1 (.out(button_1_out));
  Button button_2 (.out(button_2_out));
  Button button_3 (.out(button_3_out));
  not not_59 (not_59_out, j_k_ff_27_q);
  Hex_Digit_Display hex_digit_display_1 (.value({{3{in_9}}, or_4_out[0]}));  // open: dp
  J_K_Flip_Flop j_k_ff_27 (
    .J(and_86_out), .K(and_86_out), .clk(and_94_out), .Q(j_k_ff_27_q), .reset(or_36_out));  // open: Qn, preset
  and and_94 (and_94_out, and_88_out, not_59_out);
  Hex_Digit_Display hex_digit_display_2 (.value(or_7_out));  // open: dp
  Hex_Digit_Display hex_digit_display_3 (.value({in_8, or_21_out}));  // open: dp
  Hex_Digit_Display hex_digit_display_4 (.value(or_27_out));  // open: dp
  LED led_25 (.in(not_60_out));
  LED led_26 (.in(or_1_out));
  LED led_27 (.in(j_k_ff_27_q));
  not not_60 (not_60_out, or_1_out);

  // Notes on the sheet:
  //   The Main Clock {
  //   The Clock Switch {
  //   this is used to switch between the main and alarm clocks
  //   The Alarm Check {
  //   The Alarm Clock {
  //   Q2
  //   Tens Hours Ripple Counter
  //   this column is the tens hours sectiom
  //   Q2
  //   Full Reset
  //   Full Reset
  //   Q0
  //   1
  //   Q0
  //   1
  //   this column is the singles hours sectiom
  //   Q1
  //   2
  //   Q1
  //   2
  //   Singles Hour Ripple Counter
  //   Q2
  //   4
  //   Q2
  //   4
  //   Q2
  //   8
  //   Q2
  //   8
  //   Q0
  //   Q0
  //   Tens Minute Ripple Counter
  //   this column is the tens minutes sectiom
  //   Q1
  //   Q1
  //   Q2
  //   Q2
  //   Enable (Set)
  //   Enable (Set)
  //   Q0
  //   1
  //   Q0
  //   1
  //   this column is the singles nimutes sectiom
  //   Q1
  //   2
  //   Q1
  //   2
  //   Singles Minutes Ripple Counter
  //   Q2
  //   4
  //   this section below is used to switch between the main
  //    clock and the alarm clock. it switches using the set alarm pin
  //   Q2
  //   4
  //   Q2
  //   8
  //   Q2
  //   8
  //   Clock
  //   M+ (Increment Minutes)
  //   Hr+ (Increment Minutes)
  //   Enable Alarm
  //   Snooze Alarm
  //   used to hold the alarm state, enable/disable/snooze the alarm
  //   The Marvelous Clock
  //   AM
  //   PM
  //   Alarm
endmodule

module Stage1 (
  input  in_1,
  input  Enable__Set,
  input  in_3
);

  wire and_1_out, and_2_out, and_3_out, and_4_out, and_5_out, clock_1_out, j_k_ff_1_q, j_k_ff_2_q,
       j_k_ff_3_q, j_k_ff_4_q, j_k_ff_5_q, j_k_ff_6_q, j_k_ff_7_q;
  wire [2:0] d_ff_1_q;
  wire [3:0] d_ff_4_q;

  J_K_Flip_Flop #(.trigger("falling")) j_k_ff_1 (
    .J(Enable__Set), .K(Enable__Set), .clk(and_5_out), .Q(j_k_ff_1_q), .reset(and_2_out));  // open: Qn, preset
  LED led_1 (.in(j_k_ff_1_q));
  D_Flip_Flop d_ff_1 (.D(j_k_ff_1_q), .clk(clock_1_out), .Q(d_ff_1_q[0]));  // open: Qn, preset, reset
  J_K_Flip_Flop #(.trigger("falling")) j_k_ff_2 (
    .J(j_k_ff_1_q), .K(j_k_ff_1_q), .clk(and_5_out), .Q(j_k_ff_2_q), .reset(and_2_out));  // open: Qn, preset
  and and_1 (and_1_out, j_k_ff_1_q, j_k_ff_2_q);
  LED led_2 (.in(j_k_ff_2_q));
  D_Flip_Flop d_ff_2 (.D(j_k_ff_2_q), .clk(clock_1_out), .Q(d_ff_1_q[1]));  // open: Qn, preset, reset
  J_K_Flip_Flop #(.trigger("falling")) j_k_ff_3 (
    .J(and_1_out), .K(and_1_out), .clk(and_5_out), .Q(j_k_ff_3_q), .reset(and_2_out));  // open: Qn, preset
  and and_2 (and_2_out, j_k_ff_3_q, j_k_ff_2_q);
  LED led_3 (.in(j_k_ff_3_q));
  D_Flip_Flop d_ff_3 (.D(j_k_ff_3_q), .clk(clock_1_out), .Q(d_ff_1_q[2]));  // open: Qn, preset, reset
  Hex_Digit_Display hex_digit_display_1 (.value({in_3, d_ff_1_q}));  // open: dp
  Clock clock_1 (.out(clock_1_out));
  Hex_Digit_Display hex_digit_display_2 (.value(d_ff_4_q));  // open: dp
  J_K_Flip_Flop #(.trigger("falling")) j_k_ff_4 (
    .J(in_1), .K(in_1), .clk(clock_1_out), .Q(j_k_ff_4_q), .reset(and_5_out));  // open: Qn, preset
  LED led_4 (.in(j_k_ff_4_q));
  J_K_Flip_Flop #(.trigger("falling")) j_k_ff_5 (
    .J(j_k_ff_4_q), .K(j_k_ff_4_q), .clk(clock_1_out), .Q(j_k_ff_5_q), .reset(and_5_out));  // open: Qn, preset
  D_Flip_Flop d_ff_4 (.D(j_k_ff_4_q), .clk(clock_1_out), .Q(d_ff_4_q[0]));  // open: Qn, preset, reset
  LED led_5 (.in(j_k_ff_5_q));
  and and_3 (and_3_out, j_k_ff_4_q, j_k_ff_5_q);
  J_K_Flip_Flop #(.trigger("falling")) j_k_ff_6 (
    .J(and_3_out), .K(and_3_out), .clk(clock_1_out), .Q(j_k_ff_6_q), .reset(and_5_out));  // open: Qn, preset
  D_Flip_Flop d_ff_5 (.D(j_k_ff_5_q), .clk(clock_1_out), .Q(d_ff_4_q[1]));  // open: Qn, preset, reset
  LED led_6 (.in(j_k_ff_6_q));
  and and_4 (and_4_out, and_3_out, j_k_ff_6_q);
  J_K_Flip_Flop #(.trigger("falling")) j_k_ff_7 (
    .J(and_4_out), .K(and_4_out), .clk(clock_1_out), .Q(j_k_ff_7_q), .reset(and_5_out));  // open: Qn, preset
  D_Flip_Flop d_ff_6 (.D(j_k_ff_6_q), .clk(clock_1_out), .Q(d_ff_4_q[2]));  // open: Qn, preset, reset
  LED led_7 (.in(j_k_ff_7_q));
  D_Flip_Flop d_ff_7 (.D(j_k_ff_7_q), .clk(clock_1_out), .Q(d_ff_4_q[3]));  // open: Qn, preset, reset
  and and_5 (and_5_out, j_k_ff_7_q, j_k_ff_5_q);

  // Notes on the sheet:
  //   Q0
  //   Q1
  //   Q2
  //   Q0
  //   1
  //   Q1
  //   2
  //   Q2
  //   4
  //   Q2
  //   8
endmodule

module Ideas (
);


  // Notes on the sheet:
  //   the other idea i had for stage 5 was to use a stack to store the bits and antoher to store the Alarm time
endmodule
